// Logisim project 4-bit-cpu.circ as structural Verilog: 4 circuits, main circuit main
module main (
);

  wire CLK, CLR, DWE, SUB, WE;
  wire [1:0] AFS, RSS;
  wire [2:0] Addr_A, Addr_B, Addr_D;
  wire [3:0] A, ALU_Res, B, multiplexer_1_out, Opcode;
  wire [3:3] Data;
  wire [7:0] counter_1_q;
  wire [11:7] rom_1_data;

  Clock clock_1 (.out(CLK));
  Counter counter_1 (.Q(counter_1_q), .clk(CLK), .clr(CLR));  // open: load, D, count, carry
  Button button_1 (.out(CLR));
  ROM #(.dataWidth(16)) rom_1 (
    .addr(counter_1_q), .data({Opcode, rom_1_data[11], Addr_D, rom_1_data[7], Addr_A, Data[3], Addr_B}));  // open: sel
  ROM #(.addrWidth(4), .dataWidth(7)) rom_2 (.addr(Opcode), .data({SUB, AFS, RSS, DWE, WE}));  // open: sel
  Multiplexer #(.select(2), .width(4)) multiplexer_1 (
    .in0({Data[3], Addr_B}), .in1(ALU_Res), .in2(A), .out(multiplexer_1_out), .sel(RSS));  // open: in3, en
  TTY tty_1 (.data({A[2:0], B}), .clk(CLK), .we(DWE), .clr(CLR));
  _3_port_reg_file u_3_port_reg_file_1 (
    .Data(multiplexer_1_out), .Load(WE), .Data_Addr(Addr_D), .CLK(CLK), .Addr_A(Addr_A), .Addr_B(Addr_B),
    .A(A), .B(B), .CLR(CLR));
  alu alu_1 (.SUB(SUB), .A(A), .B(B), .AFS(AFS), .ALU_Res(ALU_Res));

  // Other names for the same wires on the sheet: Data[2:0] = Addr_B

  // Notes on the sheet:
  //   PC
  //   PROM(for Code)
  //   PROM(for Inst Decoder)
  //   contents of rom_1 (hex, n*v repeats v):
  //   1000 1101 1203 1303 3023 2420 f441 3024 7331 3023 4534 3025 5534 3025 6534 3025
  //   contents of rom_2 (hex, n*v repeats v):
  //   0 1 9 2 5 15 25 35 7*0 75
  //   WE = Register Write Enable
  //   DWE = Display Write Enable
  //   RSS = Register Source Select
  //   AFS = ALU Function Select
  //   SUB = Subtract
endmodule

module fulladder (
  input  cin,
  input  a,
  input  b,
  output res,
  output cout
);

  wire and_1_out, and_2_out, xor_1_out;

  and and_1 (and_1_out, a, b);
  xor xor_1 (xor_1_out, a, b);
  or or_1 (cout, and_1_out, and_2_out);
  and and_2 (and_2_out, cin, xor_1_out);
  xor xor_2 (res, cin, xor_1_out);
endmodule

module alu (
  input  SUB,
  input  [3:0] A,
  input  [3:0] B,
  input  [1:0] AFS,
  output [3:0] ALU_Res
);

  wire [3:0] adder_1_out, and_1_out, bit_extender_1_out, or_1_out, xor_1_out, xor_2_out;

  assign bit_extender_1_out = {{3{SUB}}, SUB};  // Bit_Extender bit_extender_1
  assign and_1_out = A & B;  // AND_Gate and_1, 4 bits wide
  assign or_1_out = A | B;  // OR_Gate or_1, 4 bits wide
  Adder #(.width(4)) adder_1 (.a(A), .b(xor_1_out), .out(adder_1_out), .cin(SUB));  // open: cout
  assign xor_1_out = B ^ bit_extender_1_out;  // XOR_Gate xor_1, 4 bits wide
  assign xor_2_out = A ^ B;  // XOR_Gate xor_2, 4 bits wide
  Multiplexer #(.select(2), .width(4)) multiplexer_1 (
    .in0(xor_2_out), .in1(and_1_out), .in2(or_1_out), .in3(adder_1_out), .out(ALU_Res), .sel(AFS));  // open: en
endmodule

module _3_port_reg_file (
  input  [3:0] Data,
  input  Load,
  input  [2:0] Addr_A,
  input  [2:0] Data_Addr,
  input  [2:0] Addr_B,
  input  CLK,
  input  CLR,
  output [3:0] A,
  output [3:0] B
);

  wire and_1_out, and_2_out, and_3_out, and_4_out, and_5_out, and_6_out, and_7_out, and_8_out,
       decoder_1_out0, decoder_1_out1, decoder_1_out2, decoder_1_out3, decoder_1_out4, decoder_1_out5,
       decoder_1_out6, decoder_1_out7;
  wire [3:0] register_1_q, register_2_q, register_3_q, register_4_q, register_5_q, register_6_q,
       register_7_q, register_8_q;

  Decoder #(.select(3)) decoder_1 (
    .out0(decoder_1_out0), .out1(decoder_1_out1), .out2(decoder_1_out2), .out3(decoder_1_out3),
    .out4(decoder_1_out4), .out5(decoder_1_out5), .out6(decoder_1_out6), .out7(decoder_1_out7),
    .sel(Data_Addr));  // open: en
  and and_1 (and_1_out, Load, decoder_1_out0);
  and and_2 (and_2_out, Load, decoder_1_out1);
  and and_3 (and_3_out, Load, decoder_1_out2);
  and and_4 (and_4_out, Load, decoder_1_out3);
  Register #(.width(4)) register_1 (.D(Data), .en(and_1_out), .Q(register_1_q), .clk(CLK), .clr(CLR));
  Register #(.width(4)) register_2 (.D(Data), .en(and_2_out), .Q(register_2_q), .clk(CLK), .clr(CLR));
  Register #(.width(4)) register_3 (.D(Data), .en(and_3_out), .Q(register_3_q), .clk(CLK), .clr(CLR));
  Register #(.width(4)) register_4 (.D(Data), .en(and_4_out), .Q(register_4_q), .clk(CLK), .clr(CLR));
  and and_5 (and_5_out, Load, decoder_1_out4);
  and and_6 (and_6_out, Load, decoder_1_out5);
  and and_7 (and_7_out, Load, decoder_1_out6);
  and and_8 (and_8_out, Load, decoder_1_out7);
  Register #(.width(4)) register_5 (.D(Data), .en(and_5_out), .Q(register_5_q), .clk(CLK), .clr(CLR));
  Register #(.width(4)) register_6 (.D(Data), .en(and_6_out), .Q(register_6_q), .clk(CLK), .clr(CLR));
  Register #(.width(4)) register_7 (.D(Data), .en(and_7_out), .Q(register_7_q), .clk(CLK), .clr(CLR));
  Register #(.width(4)) register_8 (.D(Data), .en(and_8_out), .Q(register_8_q), .clk(CLK), .clr(CLR));
  Multiplexer #(.select(3), .width(4)) multiplexer_1 (
    .in0(register_1_q), .in1(register_2_q), .in2(register_3_q), .in3(register_4_q), .in4(register_5_q),
    .in5(register_6_q), .in6(register_7_q), .in7(register_8_q), .out(A), .sel(Addr_A));  // open: en
  Multiplexer #(.select(3), .width(4)) multiplexer_2 (
    .in0(register_1_q), .in1(register_2_q), .in2(register_3_q), .in3(register_4_q), .in4(register_5_q),
    .in5(register_6_q), .in6(register_7_q), .in7(register_8_q), .out(B), .sel(Addr_B));  // open: en
endmodule
